// Logisim project Final.circ as structural Verilog: 1 circuit, main circuit main
module main (
  input  Reset
);

  wire clk, DWE, not_1_out, SUB, WE;
  wire [1:0] AFS, RSS;
  wire [2:0] AddrA, AddrB, AddrD, register1_1_p7_2;
  wire [3:0] alu_1_alu_out, multiplexer_1_out, Opcode, register1_1_p8;
  wire [3:3] register1_1_p7;
  wire [7:0] counter_1_q;
  wire [7:7] rom_1_data;
  wire [11:3] ProgramPROM_data;

  Clock u_Clk (.out(clk));
  Counter counter_1 (.clr(Reset), .load(1'b0), .up(1'b1), .count(1'b1), .clk(clk), .Q(counter_1_q));  // open: D, carry
  ROM #(.dataWidth(16)) ProgramPROM (
    .addr(counter_1_q),
    .data({Opcode, ProgramPROM_data[11], AddrD, ProgramPROM_data[7], AddrA, ProgramPROM_data[3], AddrB}));
  ROM #(.addrWidth(4)) rom_1 (.addr(Opcode), .data({rom_1_data[7], SUB, AFS, RSS, DWE, WE}));
  Multiplexer #(.select(2), .width(4), .enable("false")) multiplexer_1 (
    .in0({ProgramPROM_data[3], AddrB}), .in1({register1_1_p7[3], register1_1_p7_2}), .in2(alu_1_alu_out),
    .out(multiplexer_1_out), .sel(RSS));  // open: in3
  // Register1 register1_1: pin names not known; wires that end beside it: multiplexer_1_out, WE, AddrD, clk, AddrA, AddrB, {register1_1_p7[3], register1_1_p7_2}, register1_1_p8, register1_1_p8
  not not_1 (not_1_out, clk);
  TTY tty_1 (.data({register1_1_p7_2, register1_1_p8}), .clk(not_1_out), .we(DWE));  // open: clr
  ALU alu_1 (
    .B(register1_1_p8), .ALU_OUT(alu_1_alu_out), .Sub(SUB), .AFS(AFS),
    .A({register1_1_p7[3], register1_1_p7_2}));

  // Notes on the sheet:
  //   contents of ProgramPROM (hex, n*v repeats v):
  //   1002 1103 1200 1304 140a 1506 1601 1707 3001 3002 3034 3056 3071 1105 1409 160e 3051 3002 3033 3070
  //   3074 3053 3051 3056 100a 3020 1103 1402 1601 3036 1605 3057 3056 3010 3042 3014 3011 3020 1703 1004
  //   1102 150b 160d 140a 1300 2201 3070 3015 3071 3076 3072 3034 2200 3070 3014 3071 3076 3072 3034 1501
  //   120f 4212 2225 2202 3070 3016 3071 3076 3072 3034 f201 3070 3016 3071 3076 3072
  //   contents of rom_1 (hex, n*v repeats v):
  //   0 1 39 2 9 15 25 35 79 6*0 79
  //   Jase Dryden
endmodule
